// Digital circuit cmos_implementation_NOR_gate.dig as structural Verilog
module cmos_implementation_NOR_gate (
  input  A,
  input  B,
  output Y
);

  wire pfet_1_d;

  NFET nfet_1 (.G(A), .D(Y), .S(1'b0));
  PFET pfet_1 (.G(B), .S(1'b1), .D(pfet_1_d));
  PFET pfet_2 (.G(A), .S(pfet_1_d), .D(Y));
  NFET nfet_2 (.G(B), .D(Y), .S(1'b0));
endmodule
