// Digital circuit cmos_implementation_OR_gate.dig as structural Verilog
module cmos_implementation_OR_gate (
  input  in_0,
  input  in_1,
  output out_0
);

  wire pfet_1_d;

  NFET nfet_1 (.G(in_0), .D(out_0), .S(1'b1));
  PFET pfet_1 (.G(in_1), .S(1'b0), .D(pfet_1_d));
  PFET pfet_2 (.G(in_0), .S(pfet_1_d), .D(out_0));
  NFET nfet_2 (.G(in_1), .D(out_0), .S(1'b1));
endmodule
