// Digital circuit par_b_alternative_2.dig as structural Verilog
module par_b_alternative_2 (
  input  in_0,
  input  in_1,
  input  in_2,
  output out_0
);

  wire and_1_out, and_2_out, and_3_out;

  and and_1 (and_1_out, ~in_0, ~in_2);  // And
  and and_2 (and_2_out, in_0, ~in_1, ~in_2);  // And
  and and_3 (and_3_out, in_0, in_1);
  or or_1 (out_0, and_1_out, and_2_out, and_3_out);
endmodule
