// Digital circuit part_c.dig as structural Verilog
module part_c (
  input  in_0,
  input  in_1,
  input  in_2,
  output out_0
);

  wire nfet_1_s, nfet_2_s, nfet_4_d, nfet_7_d, pfet_1_d, pfet_4_d, pfet_6_d, pfet_7_d;

  PFET pfet_1 (.G(in_0), .S(1'b1), .D(pfet_1_d));
  NFET nfet_1 (.G(in_0), .D(pfet_1_d), .S(nfet_1_s));
  PFET pfet_2 (.G(in_1), .S(1'b1), .D(pfet_1_d));
  NFET nfet_2 (.G(in_1), .D(nfet_1_s), .S(nfet_2_s));
  PFET pfet_3 (.G(in_2), .S(1'b1), .D(pfet_1_d));
  NFET nfet_3 (.G(in_2), .D(nfet_2_s), .S(1'b0));
  NFET nfet_4 (.G(in_0), .D(nfet_4_d), .S(1'b0));
  PFET pfet_4 (.G(in_1), .S(1'b1), .D(pfet_4_d));
  PFET pfet_5 (.G(in_0), .S(pfet_4_d), .D(nfet_4_d));
  NFET nfet_5 (.G(in_1), .D(nfet_4_d), .S(1'b0));
  PFET pfet_6 (.G(pfet_1_d), .S(1'b1), .D(pfet_6_d));
  NFET nfet_6 (.G(pfet_1_d), .D(pfet_6_d), .S(1'b0));
  NFET nfet_7 (.G(pfet_6_d), .D(nfet_7_d), .S(1'b0));
  PFET pfet_7 (.G(nfet_4_d), .S(1'b1), .D(pfet_7_d));
  PFET pfet_8 (.G(pfet_6_d), .S(pfet_7_d), .D(nfet_7_d));
  NFET nfet_8 (.G(nfet_4_d), .D(nfet_7_d), .S(1'b0));
  PFET pfet_9 (.G(nfet_7_d), .S(1'b1), .D(out_0));
  NFET nfet_9 (.G(nfet_7_d), .D(out_0), .S(1'b0));
endmodule

/* Test case part_c_test:
in_0 in_1 in_2  out_0
  0    0    0      1
  0    0    1      1
  0    1    0      0
  0    1    1      0
  1    0    0      0 
  1    0    1      0
  1    1    0      0
  1    1    1      1
*/
