// Digital circuit part_c_commit_1.dig as structural Verilog
module part_c_commit_1 (
  input  in_0,
  input  in_1,
  input  in_2,
  output x_1,
  output x_0,
  output x_2,
  output out_0
);

  wire nfet_1_s, nfet_2_s, pfet_4_d, pfet_7_d;

  PFET pfet_1 (.G(in_0), .S(1'b1), .D(x_0));
  NFET nfet_1 (.G(in_0), .D(x_0), .S(nfet_1_s));
  PFET pfet_2 (.G(in_1), .S(1'b1), .D(x_0));
  NFET nfet_2 (.G(in_1), .D(nfet_1_s), .S(nfet_2_s));
  PFET pfet_3 (.G(in_2), .S(1'b1), .D(x_0));
  NFET nfet_3 (.G(in_2), .D(nfet_2_s), .S(1'b0));
  NFET nfet_4 (.G(in_0), .D(x_1), .S(1'b0));
  PFET pfet_4 (.G(in_1), .S(1'b1), .D(pfet_4_d));
  PFET pfet_5 (.G(in_0), .S(pfet_4_d), .D(x_1));
  NFET nfet_5 (.G(in_1), .D(x_1), .S(1'b0));
  PFET pfet_6 (.G(x_0), .S(1'b1), .D(x_2));
  NFET nfet_6 (.G(x_0), .D(x_2), .S(1'b0));
  PFET pfet_7 (.G(x_1), .S(1'b0), .D(pfet_7_d));
  PFET pfet_8 (.G(x_2), .S(pfet_7_d), .D(out_0));
  NFET nfet_7 (.G(x_2), .D(out_0), .S(1'b1));
  NFET nfet_8 (.G(x_1), .D(out_0), .S(1'b1));

  // Notes on the sheet:
  //   x_0: SkrrtMoney
endmodule

/* Test case part_c_test:
in_0 in_1 in_2  out_0
  0    0    0      1
  0    0    1      1
  0    1    0      0
  0    1    1      0
  1    0    0      0 
  1    0    1      0
  1    1    0      0
  1    1    1      1
*/
