// Digital circuit playWithLED_Display.dig as structural Verilog
module playWithLED_Display (
  input  seg_a,
  input  seg_b,
  input  seg_c,
  input  seg_d,
  input  seg_e,
  input  seg_f,
  input  seg_g,
  input  seg_dp
);

  Seven_Seg seven_seg_1 (.a(seg_a), .b(seg_b), .c(seg_c), .d(seg_d), .e(seg_e), .f(seg_f), .g(seg_g), .dp(seg_dp));
endmodule
