// Digital circuit playWithTunnels.dig as structural Verilog
module playWithTunnels (
  input  input_with_Tunnel,
  input  input_without_Tunnel,
  output out
);

  and and_1 (out, input_with_Tunnel, input_without_Tunnel);

  // Other names for the same wires on the sheet: wire1 = input_with_Tunnel

  // Notes on the sheet:
  //   Note how both the 2 tunnels in the circuit have the same name "wire1". 
  //   This signifies electrical connectivity
endmodule
