// Digital circuit complement_2_negative_lab2_part2_commit_1.dig as structural Verilog
module complement_2_negative_lab2_part2_commit_1 (
  input  in_5,
  input  in_6,
  input  in_7,
  input  in_8,
  output out_1,
  output out_2,
  output out_3,
  output out_4
);

  wire and_1_out, and_2_out, and_3_out, and_4_out, and_5_out, not_1_out, not_2_out, not_3_out, not_4_out,
       or_1_out, or_2_out, xor_2_out, xor_4_out, xor_5_out;

  not not_1 (not_1_out, in_5);
  not not_2 (not_2_out, in_6);
  not not_3 (not_3_out, in_7);
  not not_4 (not_4_out, in_8);
  xor xor_1 (out_1, not_1_out, 1'b1);
  and and_1 (and_1_out, not_1_out, 1'b1);
  xor xor_2 (xor_2_out, not_2_out, 1'b0);
  and and_2 (and_2_out, not_2_out, 1'b0);
  xor xor_3 (out_2, and_1_out, xor_2_out);
  and and_3 (and_3_out, xor_2_out, and_1_out);
  xor xor_4 (xor_4_out, not_3_out, 1'b0);
  and and_4 (and_4_out, not_3_out, 1'b0);
  xor xor_5 (xor_5_out, not_4_out, 1'b0);
  or or_1 (or_1_out, and_3_out, and_2_out);
  and and_5 (and_5_out, or_1_out, xor_4_out);
  xor xor_6 (out_3, or_1_out, xor_4_out);
  or or_2 (or_2_out, and_5_out, and_4_out);
  xor xor_7 (out_4, or_2_out, xor_5_out);
endmodule
