// Digital circuit complement_2_negative_lab2_part2_commit_2.dig as structural Verilog
module complement_2_negative_lab2_part2_commit_2 (
  input  in_1,
  input  in_2,
  input  in_3,
  input  in_4,
  output out_5,
  output out_6,
  output out_7,
  output out_8
);

  wire and_1_out, and_2_out, and_3_out, xor_1_out, xor_2_out, xor_3_out, xor_4_out;

  xor xor_1 (xor_1_out, in_1, in_4);
  xor xor_2 (xor_2_out, in_2, in_4);
  xor xor_3 (xor_3_out, in_3, in_4);
  xor xor_4 (xor_4_out, in_4, in_4);
  xor xor_5 (out_5, xor_1_out, in_4);
  and and_1 (and_1_out, xor_1_out, in_4);
  xor xor_6 (out_6, and_1_out, xor_2_out);
  and and_2 (and_2_out, and_1_out, xor_2_out);
  xor xor_7 (out_7, and_2_out, xor_3_out);
  and and_3 (and_3_out, and_2_out, xor_3_out);
  xor xor_8 (out_8, and_3_out, xor_4_out);
endmodule
