// Digital circuit lab2_part2_commit_1.dig as structural Verilog
module lab2_part2_commit_1 (
  input  in0,
  input  in1,
  input  in2,
  input  in3,
  output seg_a,
  output seg_f,
  output seg_b,
  output seg_g,
  output seg_e,
  output seg_c,
  output seg_d,
  output seg_dp,
  output sign_a,
  output sign_f,
  output sign_b,
  output sign_g,
  output sign_e,
  output sign_c,
  output sign_d,
  output sign_dp
);

  wire and_2_out, and_3_out, and_4_out, out0, out1, out2, out3, outNo0, outNo1, outNo2, outNo3, outNo4,
       outNo5, outNo6, outNo7, outNo8, xor_1_out, xor_2_out, xor_3_out, xor_4_out;

  Seven_Seg seven_seg_1 (.a(1'b0), .b(1'b0), .c(1'b0), .d(1'b0), .e(1'b0), .f(1'b0), .g(in3), .dp(1'b0));
  Seven_Seg seven_seg_2 (.a(seg_a), .b(seg_a), .c(seg_a), .d(seg_a), .e(seg_a), .f(seg_a), .g(seg_a), .dp(1'b0));
  and and_1 (seg_a, ~out0, ~out1, ~out2, out3);  // And
  or or_1 (seg_a, outNo0, outNo2, outNo3, outNo5, outNo7, outNo8);
  or or_2 (seg_a, outNo0, outNo1, outNo2, outNo3, outNo4, outNo7, outNo8);
  xor xor_1 (xor_1_out, in0, in3);
  xor xor_2 (xor_2_out, in1, in3);
  xor xor_3 (xor_3_out, in2, in3);
  xor xor_4 (xor_4_out, in3, in3);
  or or_3 (seg_a, outNo0, outNo1, outNo3, outNo4, outNo5, outNo6, outNo7, outNo8);
  xor xor_5 (out0, xor_1_out, in3);
  and and_2 (and_2_out, xor_1_out, in3);
  xor xor_6 (out1, and_2_out, xor_2_out);
  and and_3 (and_3_out, and_2_out, xor_2_out);
  or or_4 (seg_a, outNo0, outNo2, outNo3, outNo5, outNo6, outNo8);
  xor xor_7 (out2, and_3_out, xor_3_out);
  and and_4 (and_4_out, and_3_out, xor_3_out);
  or or_5 (seg_a, outNo0, outNo2, outNo6, outNo8);
  or or_6 (seg_a, outNo0, outNo4, outNo5, outNo6, outNo8);
  xor xor_8 (out3, and_4_out, xor_4_out);
  or or_7 (seg_a, outNo2, outNo3, outNo4, outNo5, outNo6, outNo8);
  Decoder #(.Selector_Bits(3)) decoder_1 (
    .sel({out2, out1, out0}), .out_0(outNo0), .out_1(outNo1), .out_2(outNo2), .out_3(outNo3), .out_4(outNo4),
    .out_5(outNo5), .out_6(outNo6), .out_7(outNo7));

  assign seg_b = seg_a;
  assign seg_c = seg_a;
  assign seg_d = seg_a;
  assign seg_dp = 1'b0;
  assign seg_e = seg_a;
  assign seg_f = seg_a;
  assign seg_g = seg_a;
  assign sign_a = 1'b0;
  assign sign_b = 1'b0;
  assign sign_c = 1'b0;
  assign sign_d = 1'b0;
  assign sign_dp = 1'b0;
  assign sign_e = 1'b0;
  assign sign_f = 1'b0;
  assign sign_g = in3;

  // Notes on the sheet:
  //   Interface (do not edit the content inside this box)
  //   Outputs:
  //   Inputs
  //   Sign
  //   Decimal Number
endmodule

/* Test case:
in3 in2 in1 in0  sign_a sign_b sign_c sign_d sign_e sign_f sign_g  seg_a seg_b seg_c seg_d seg_e seg_f seg_g
 0   0   0   0    0      0      0      0      0      0      0       1     1     1     1     1     1     0
*/
