// Digital circuit lab2_part2_first_part_working.dig as structural Verilog
module lab2_part2_first_part_working (
  input  in0,
  input  in1,
  input  in2,
  input  in3,
  output seg_a,
  output seg_f,
  output seg_b,
  output seg_g,
  output seg_e,
  output seg_c,
  output seg_d,
  output seg_dp,
  output sign_a,
  output sign_f,
  output sign_b,
  output sign_g,
  output sign_e,
  output sign_c,
  output sign_d,
  output sign_dp,
  output out_21,
  output out_22,
  output out_23,
  output out_24
);

  wire and_1_out, and_2_out, and_3_out, xor_1_out, xor_2_out, xor_3_out, xor_4_out;

  Seven_Seg seven_seg_1 (.a(1'b0), .b(1'b0), .c(1'b0), .d(1'b0), .e(1'b0), .f(1'b0), .g(in3), .dp(1'b0));
  Seven_Seg seven_seg_2 (.a(out_24), .b(out_24), .c(out_24), .d(out_24), .e(out_24), .f(out_24), .g(out_24), .dp(1'b0));
  xor xor_1 (xor_1_out, in0, in3);
  xor xor_2 (xor_2_out, in1, in3);
  xor xor_3 (xor_3_out, in2, in3);
  xor xor_4 (xor_4_out, in3, in3);
  xor xor_5 (out_21, xor_1_out, in3);
  and and_1 (and_1_out, xor_1_out, in3);
  xor xor_6 (out_22, and_1_out, xor_2_out);
  and and_2 (and_2_out, and_1_out, xor_2_out);
  xor xor_7 (out_23, and_2_out, xor_3_out);
  and and_3 (and_3_out, and_2_out, xor_3_out);
  xor xor_8 (out_24, and_3_out, xor_4_out);

  assign seg_a = out_24;
  assign seg_b = out_24;
  assign seg_c = out_24;
  assign seg_d = out_24;
  assign seg_dp = 1'b0;
  assign seg_e = out_24;
  assign seg_f = out_24;
  assign seg_g = out_24;
  assign sign_a = 1'b0;
  assign sign_b = 1'b0;
  assign sign_c = 1'b0;
  assign sign_d = 1'b0;
  assign sign_dp = 1'b0;
  assign sign_e = 1'b0;
  assign sign_f = 1'b0;
  assign sign_g = in3;

  // Other names for the same wires on the sheet: out0 = out_21; out1 = out_22; out2 = out_23; out3 = out_24

  // Notes on the sheet:
  //   Interface (do not edit the content inside this box)
  //   Outputs:
  //   Inputs
  //   Sign
  //   Decimal Number
endmodule

/* Test case:
in3 in2 in1 in0  sign_a sign_b sign_c sign_d sign_e sign_f sign_g  seg_a seg_b seg_c seg_d seg_e seg_f seg_g
 0   0   0   0    0      0      0      0      0      0      0       1     1     1     1     1     1     0
*/
