// Digital circuit lab2_part2_initial.dig as structural Verilog
module lab2_part2_initial (
  input  in0,
  input  in1,
  input  in2,
  input  in3,
  output seg_a,
  output seg_f,
  output seg_b,
  output seg_g,
  output seg_e,
  output seg_c,
  output seg_d,
  output seg_dp,
  output sign_a,
  output sign_f,
  output sign_b,
  output sign_g,
  output sign_e,
  output sign_c,
  output sign_d,
  output sign_dp,
  output out_21,
  output out_22,
  output out_23,
  output out_24
);

  wire and_1_out, and_2_out, and_3_out, and_4_out, and_5_out, not_1_out, not_2_out, not_3_out, not_4_out,
       or_1_out, or_2_out, xor_2_out, xor_4_out, xor_5_out;

  Seven_Seg seven_seg_1 (
    .a(sign_a), .b(sign_b), .c(sign_c), .d(sign_d), .e(sign_e), .f(sign_f), .g(sign_g), .dp(sign_dp));
  Seven_Seg seven_seg_2 (.a(seg_a), .b(seg_b), .c(seg_c), .d(seg_d), .e(seg_e), .f(seg_f), .g(seg_g), .dp(seg_dp));
  not not_1 (not_1_out, in0);
  not not_2 (not_2_out, in2);
  not not_3 (not_3_out, in3);
  not not_4 (not_4_out, in1);
  xor xor_1 (out_21, not_1_out, 1'b1);
  and and_1 (and_1_out, not_1_out, 1'b1);
  xor xor_2 (xor_2_out, not_2_out, 1'b0);
  and and_2 (and_2_out, not_2_out, 1'b0);
  xor xor_3 (out_22, and_1_out, xor_2_out);
  and and_3 (and_3_out, xor_2_out, and_1_out);
  xor xor_4 (xor_4_out, not_3_out, 1'b0);
  and and_4 (and_4_out, not_3_out, 1'b0);
  xor xor_5 (xor_5_out, not_4_out, 1'b0);
  or or_1 (or_1_out, and_3_out, and_2_out);
  and and_5 (and_5_out, or_1_out, xor_4_out);
  xor xor_6 (out_23, or_1_out, xor_4_out);
  or or_2 (or_2_out, and_5_out, and_4_out);
  xor xor_7 (out_24, or_2_out, xor_5_out);

  // Notes on the sheet:
  //   Interface (do not edit the content inside this box)
  //   Outputs:
  //   Inputs
  //   Sign
  //   Decimal Number
endmodule

/* Test case:
in3 in2 in1 in0  sign_a sign_b sign_c sign_d sign_e sign_f sign_g  seg_a seg_b seg_c seg_d seg_e seg_f seg_g
 0   0   0   0    0      0      0      0      0      0      0       1     1     1     1     1     1     0
*/
