// Digital circuit lab2_part2_multiplexer_solution_part2.dig as structural Verilog
module lab2_part2_multiplexer_solution_part2 (
);

  wire out0, out1, out2, outNo0, outNo1, outNo2, outNo3, outNo4, outNo5, outNo6, outNo7, outNo8, seg_a,
       seg_b, seg_c, seg_d, seg_e, seg_f, seg_g;

  or or_1 (seg_a, outNo0, outNo2, outNo3, outNo5, outNo7, outNo8);
  or or_2 (seg_b, outNo0, outNo1, outNo2, outNo3, outNo4, outNo7, outNo8);
  or or_3 (seg_c, outNo0, outNo1, outNo3, outNo4, outNo5, outNo6, outNo7, outNo8);
  or or_4 (seg_d, outNo0, outNo2, outNo3, outNo5, outNo6, outNo8);
  or or_5 (seg_e, outNo0, outNo2, outNo6, outNo8);
  or or_6 (seg_f, outNo0, outNo4, outNo5, outNo6, outNo8);
  or or_7 (seg_g, outNo2, outNo3, outNo4, outNo5, outNo6, outNo8);
  Decoder #(.Selector_Bits(3)) decoder_1 (
    .sel({out2, out1, out0}), .out_0(outNo0), .out_1(outNo1), .out_2(outNo2), .out_3(outNo3), .out_4(outNo4),
    .out_5(outNo5), .out_6(outNo6), .out_7(outNo7));
endmodule
