// Digital circuit lab2_part3_commit_1.dig as structural Verilog
module lab2_part3_commit_1 (
  input  A_3,
  input  A_2,
  input  A_1,
  input  A_0,
  input  clk,
  input  clk_2,
  input  in0,
  input  in1,
  input  in2,
  input  in3,
  input  sel_write_1,
  input  sel_write_0,
  input  sel_readA_1,
  input  sel_readA_0,
  input  sel_readB_1,
  input  sel_readB_0,
  output Ar_1,
  output Ar_2,
  output Ar_3,
  output Ar_0
);

  wire multiplexer_1_out;
  wire [3:0] demultiplexer_1_out_0, demultiplexer_1_out_1, demultiplexer_1_out_2, demultiplexer_1_out_3,
       Reg0_q, Reg1_q, Reg2_q, Reg3_q;

  Seven_Seg_Hex seven_seg_hex_1 (.d({in3, in2, in1, in0}), .dp(1'b0));
  Demultiplexer #(.Selector_Bits(2)) demultiplexer_1 (
    .sel({sel_write_1, sel_write_0}), .in(in0), .out_0(demultiplexer_1_out_0[0]),
    .out_1(demultiplexer_1_out_1[0]), .out_2(demultiplexer_1_out_2[0]), .out_3(demultiplexer_1_out_3[0]));
  Register #(.Bits(4)) Reg0 (.D(demultiplexer_1_out_0), .C(clk_2), .en(1'b1), .Q(Reg0_q));
  Register #(.Bits(4)) Reg1 (.D(demultiplexer_1_out_1), .C(clk_2), .en(1'b1), .Q(Reg1_q));
  Register #(.Bits(4)) Reg2 (.D(demultiplexer_1_out_2), .C(clk_2), .en(1'b1), .Q(Reg2_q));
  Register #(.Bits(4)) Reg3 (.D(demultiplexer_1_out_3), .C(clk_2), .en(1'b1), .Q(Reg3_q));
  Multiplexer #(.Selector_Bits(2)) multiplexer_1 (
    .sel({sel_readA_1, sel_readA_0}), .in_0(Reg0_q[0]), .in_1(Reg1_q[0]), .in_2(Reg2_q[0]), .in_3(Reg3_q[0]),
    .out(multiplexer_1_out));
  Seven_Seg_Hex seven_seg_hex_2 (.d({2'b00, sel_write_1, sel_write_0}), .dp(1'b0));
  Seven_Seg_Hex seven_seg_hex_3 (.d({2'b00, sel_readA_1, sel_readA_0}), .dp(1'b0));
  Register #(.Bits(4)) register_1 (.D({A_0, A_1, A_2, A_3}), .C(clk), .en(1'b1), .Q({Ar_3, Ar_2, Ar_1, Ar_0}));
  Seven_Seg_Hex seven_seg_hex_4 (.d({2'b00, sel_readB_1, sel_readB_0}), .dp(1'b0));
  // Pins of 1 and 4 bits meet at {in3, in2, in1, in0}
  // Pins of 1 and 4 bits meet at demultiplexer_1_out_3
  // Pins of 1 and 4 bits meet at Reg3_q
  // Pins of 1 and 4 bits meet at demultiplexer_1_out_2
  // Pins of 1 and 4 bits meet at Reg2_q
  // Pins of 1 and 4 bits meet at demultiplexer_1_out_1
  // Pins of 1 and 4 bits meet at Reg1_q
  // Pins of 1 and 4 bits meet at demultiplexer_1_out_0
  // Pins of 1 and 4 bits meet at Reg0_q

  // Other names for the same wires on the sheet: clk_t = clk_2

  // Notes on the sheet:
  //   Keypad
  //   Synchronizing Clock
  //   Register Selection: Write-to
  //   Register Selection: Read-from
  //   ALU input A register address:
  //   ALU input B register address:
endmodule
