// Digital circuit lab2_part3_initial.dig as structural Verilog
module lab2_part3_initial (
  input  A_3,
  input  A_2,
  input  A_1,
  input  A_0,
  input  clk,
  input  in_10,
  input  clk_2,
  input  in0,
  input  in1,
  input  in2,
  input  in3,
  input  sel_write_1,
  input  sel_write_0,
  input  sel_readA_1,
  input  sel_readA_0,
  input  sel_readB_1,
  input  sel_readB_0,
  output Ar_1,
  output Ar_2,
  output Ar_3,
  output Ar_0
);

  Seven_Seg_Hex seven_seg_hex_1 (.d({in3, in2, in1, in0}), .dp(1'b0));
  Seven_Seg_Hex seven_seg_hex_2 (.d({2'b00, sel_write_1, sel_write_0}), .dp(1'b0));
  Seven_Seg_Hex seven_seg_hex_3 (.d({2'b00, sel_readA_1, sel_readA_0}), .dp(1'b0));
  Register #(.Bits(4)) register_1 (.D({A_0, A_1, A_2, A_3}), .C(clk), .en(in_10), .Q({Ar_3, Ar_2, Ar_1, Ar_0}));
  Seven_Seg_Hex seven_seg_hex_4 (.d({2'b00, sel_readB_1, sel_readB_0}), .dp(1'b0));

  // Other names for the same wires on the sheet: clk_t = clk_2

  // Notes on the sheet:
  //   Keypad
  //   Synchronizing Clock
  //   Register Selection: Write-to
  //   Register Selection: Read-from
  //   ALU input A register address:
  //   ALU input B register address:
endmodule
