// Digital circuit lab3_part3_old_b4_transfer.dig as structural Verilog
module lab3_part3_old_b4_transfer (
  input  clk,
  input  in0,
  input  in1,
  input  in2,
  input  in3,
  input  sel_write_1,
  input  sel_write_0,
  input  sel_readA_1,
  input  sel_readA_0,
  input  sel_readB_1,
  input  sel_readB_0
);

  wire inA_0, inA_1, inA_2, inA_3, inB_0, inB_1, inB_2, inB_3, out0, out1, out2, out3, reg0_0, reg0_1,
       reg0_2, reg0_3, reg1_0, reg1_1, reg1_2, reg1_3, reg2_0, reg2_1, reg2_2, reg2_3, reg3_0, reg3_1,
       reg3_2, reg3_3;
  wire [3:0] demultiplexer_1_out_0, demultiplexer_1_out_1, demultiplexer_1_out_2, demultiplexer_1_out_3;

  Seven_Seg_Hex seven_seg_hex_1 (.d({in3, in2, in1, in0}), .dp(1'b0));
  Demultiplexer #(.Selector_Bits(2)) demultiplexer_1 (
    .sel({sel_write_1, sel_write_0}), .in(in0), .out_0(demultiplexer_1_out_0[0]),
    .out_1(demultiplexer_1_out_1[0]), .out_2(demultiplexer_1_out_2[0]), .out_3(demultiplexer_1_out_3[0]));
  Register #(.Bits(4)) Reg0 (.D(demultiplexer_1_out_0), .C(clk), .en(1'b1), .Q({reg0_3, reg0_2, reg0_1, reg0_0}));
  Register #(.Bits(4)) Reg1 (.D(demultiplexer_1_out_1), .C(clk), .en(1'b1), .Q({reg1_3, reg1_2, reg1_1, reg1_0}));
  Register #(.Bits(4)) Reg2 (.D(demultiplexer_1_out_2), .C(clk), .en(1'b1), .Q({reg2_3, reg2_2, reg2_1, reg2_0}));
  Register #(.Bits(4)) Reg3 (.D(demultiplexer_1_out_3), .C(clk), .en(1'b1), .Q({reg3_3, reg3_2, reg3_1, reg3_0}));
  Multiplexer #(.Selector_Bits(2)) multiplexer_1 (
    .sel({sel_readA_1, sel_readA_0}), .in_0(reg0_0), .in_1(reg1_0), .in_2(reg2_0), .in_3(reg3_0), .out(inA_0));
  Multiplexer #(.Selector_Bits(2)) multiplexer_2 (
    .sel({sel_readB_1, sel_readB_0}), .in_0(reg0_0), .in_1(reg1_0), .in_2(reg2_0), .in_3(reg3_0), .out(inB_0));
  Seven_Seg_Hex seven_seg_hex_2 (.d({2'b00, sel_write_1, sel_write_0}), .dp(1'b0));
  Multiplexer #(.Selector_Bits(2)) multiplexer_3 (
    .sel({inB_1, inB_0}), .in_0(inA_3), .in_1(inA_2), .in_2(inA_1), .in_3(inA_0), .out(out3));
  Seven_Seg_Hex seven_seg_hex_3 (.d({2'b00, sel_readA_1, sel_readA_0}), .dp(1'b0));
  Multiplexer #(.Selector_Bits(2)) multiplexer_4 (
    .sel({inB_1, inB_0}), .in_0(inA_2), .in_1(inA_1), .in_2(inA_0), .in_3(inA_3), .out(out2));
  Multiplexer #(.Selector_Bits(2)) multiplexer_5 (
    .sel({inB_1, inB_0}), .in_0(inA_1), .in_1(inA_0), .in_2(inA_3), .in_3(inA_2), .out(out1));
  Seven_Seg_Hex seven_seg_hex_4 (.d({2'b00, sel_readB_1, sel_readB_0}), .dp(1'b0));
  Multiplexer #(.Selector_Bits(2)) multiplexer_6 (
    .sel({inB_1, inB_0}), .in_0(inA_0), .in_1(inA_3), .in_2(inA_2), .in_3(inA_1), .out(out0));
  // Pins of 1 and 4 bits meet at {in3, in2, in1, in0}
  // Pins of 1 and 4 bits meet at demultiplexer_1_out_3
  // Pins of 1 and 4 bits meet at {reg3_3, reg3_2, reg3_1, reg3_0}
  // Pins of 1 and 4 bits meet at demultiplexer_1_out_2
  // Pins of 1 and 4 bits meet at {reg2_3, reg2_2, reg2_1, reg2_0}
  // Pins of 1 and 4 bits meet at demultiplexer_1_out_1
  // Pins of 1 and 4 bits meet at {reg1_3, reg1_2, reg1_1, reg1_0}
  // Pins of 1 and 4 bits meet at demultiplexer_1_out_0
  // Pins of 1 and 4 bits meet at {reg0_3, reg0_2, reg0_1, reg0_0}
  // Pins of 1 and 4 bits meet at {inA_3, inA_2, inA_1, inA_0}
  // Pins of 1 and 4 bits meet at {inB_3, inB_2, inB_1, inB_0}

  // Notes on the sheet:
  //   Keypad
  //   Synchronizing Clock
  //   Register Selection: Write-to
  //   Register Selection: Read-from
  //   ALU input A register address:
  //   ALU input B register address:
endmodule
