// Digital circuit old_stuff_from_lab2_part2.dig as structural Verilog
module old_stuff_from_lab2_part2 (
);

  wire out0, out1, out2, out3, seg_a;

  and and_1 (seg_a, ~out0, ~out1, ~out2, ~out3);  // And
  and and_2 (seg_a, out0, ~out1, ~out2, ~out3);  // And
  and and_3 (seg_a, ~out0, out1, ~out2, ~out3);  // And
  and and_4 (seg_a, out0, out1, ~out2, ~out3);  // And
  and and_5 (seg_a, ~out0, ~out1, out2, ~out3);  // And
  not not_1 (seg_a, seg_a);
  not not_2 (seg_a, seg_a);
  not not_3 (seg_a, seg_a);
  not not_4 (seg_a, seg_a);
  not not_5 (seg_a, seg_a);
  not not_6 (seg_a, seg_a);
  not not_7 (seg_a, seg_a);
  not not_8 (seg_a, seg_a);
  not not_9 (seg_a, seg_a);
  not not_10 (seg_a, seg_a);
  not not_11 (seg_a, seg_a);
  not not_12 (seg_a, seg_a);
  not not_13 (seg_a, seg_a);
  and and_6 (seg_a, out0, ~out1, out2, ~out3);  // And
  and and_7 (seg_a, ~out0, out1, out2, ~out3);  // And
  and and_8 (seg_a, out0, out1, out2, ~out3);  // And
  not not_14 (seg_a, seg_a);
  not not_15 (seg_a, seg_a);
  not not_16 (seg_a, seg_a);
  not not_17 (seg_a, seg_a);
  not not_18 (seg_a, seg_a);
  not not_19 (seg_a, seg_a);
  not not_20 (seg_a, seg_a);
  not not_21 (seg_a, seg_a);
  and and_9 (seg_a, out0, ~out1, ~out2);  // And
  and and_10 (seg_a, ~out0, out1, ~out2);  // And
  and and_11 (seg_a, out0, out1, ~out2);  // And
  and and_12 (seg_a, ~out0, ~out1, out2);  // And
  and and_13 (seg_a, out0, ~out1, out2);  // And
  and and_14 (seg_a, ~out0, out1, out2);  // And
  and and_15 (seg_a, out0, out1, out2);
  and and_16 (seg_a, ~out0, ~out1, ~out2);  // And
  not not_22 (seg_a, seg_a);
  not not_23 (seg_a, seg_a);
  not not_24 (seg_a, seg_a);
  not not_25 (seg_a, seg_a);
  not not_26 (seg_a, seg_a);
  not not_27 (seg_a, seg_a);
  not not_28 (seg_a, seg_a);
  not not_29 (seg_a, seg_a);
  not not_30 (seg_a, seg_a);
  not not_31 (seg_a, seg_a);
  not not_32 (seg_a, seg_a);
  not not_33 (seg_a, seg_a);
  not not_34 (seg_a, seg_a);
  not not_35 (seg_a, seg_a);
  not not_36 (seg_a, seg_a);
  not not_37 (seg_a, seg_a);
  not not_38 (seg_a, seg_a);
  not not_39 (seg_a, seg_a);
  not not_40 (seg_a, seg_a);
  not not_41 (seg_a, seg_a);
  not not_42 (seg_a, seg_a);
  Demultiplexer #(.Selector_Bits(3)) demultiplexer_1 (
    .sel({out2, out1, out0}), .in(1'b1), .out_0(seg_a), .out_1(seg_a), .out_2(seg_a), .out_3(seg_a),
    .out_4(seg_a), .out_5(seg_a), .out_6(seg_a), .out_7(seg_a));

  // Other names for the same wires on the sheet: seg_b = seg_a; seg_c = seg_a; seg_d = seg_a; seg_e = seg_a;
  //   seg_f = seg_a; seg_g = seg_a
endmodule
