// Digital circuit AND_gate_CMOS.dig as structural Verilog
module AND_gate_CMOS (
  input  in_1,
  input  in_2,
  output out_3
);

  wire nfet_1_s;

  PFET pfet_1 (.G(in_1), .S(1'b0), .D(out_3));
  NFET nfet_1 (.G(in_1), .D(out_3), .S(nfet_1_s));
  NFET nfet_2 (.G(in_2), .D(nfet_1_s), .S(1'b1));
  PFET pfet_2 (.G(in_2), .S(1'b0), .D(out_3));
endmodule
