// Digital circuit cmos_implementation_AND_gate.dig as structural Verilog
module cmos_implementation_AND_gate (
  input  in_0,
  input  in_1,
  output temporaryout_0,
  output out_0
);

  wire nfet_1_s;

  PFET pfet_1 (.G(in_0), .S(1'b1), .D(temporaryout_0));
  NFET nfet_1 (.G(in_0), .D(temporaryout_0), .S(nfet_1_s));
  NFET nfet_2 (.G(in_1), .D(nfet_1_s), .S(1'b0));
  PFET pfet_2 (.G(in_1), .S(1'b1), .D(temporaryout_0));
  PFET pfet_3 (.G(temporaryout_0), .S(1'b1), .D(out_0));
  NFET nfet_3 (.G(temporaryout_0), .D(out_0), .S(1'b0));

  // Notes on the sheet:
  //   temporaryout_0: SkrrtMoney
endmodule
