// Digital circuit cmos_implementation_NAND_gate.dig as structural Verilog
module cmos_implementation_NAND_gate (
  input  in_1,
  input  in_0,
  output out_0
);

  wire fgnfet_1_s;

  PFET pfet_1 (.G(in_0), .S(1'b1), .D(out_0));
  FGNFET fgnfet_1 (.G(in_0), .D(out_0), .S(fgnfet_1_s));
  FGNFET fgnfet_2 (.G(in_1), .D(fgnfet_1_s), .S(1'b0));
  PFET pfet_2 (.G(in_1), .S(1'b1), .D(out_0));
endmodule
