// Digital circuit cmos_implementation_XOR_gate_no_pow_supp.dig as structural Verilog
module cmos_implementation_XOR_gate_no_pow_supp (
  input  in_0,
  input  in_1,
  output out_0
);

  wire fgnfet_1_s;

  PFET pfet_1 (.G(in_1), .S(in_0), .D(out_0));
  FGNFET fgnfet_1 (.G(in_1), .D(out_0), .S(fgnfet_1_s));
  FGNFET fgnfet_2 (.G(fgnfet_1_s), .D(out_0), .S(in_1));
  PFET pfet_2 (.G(in_0), .S(in_1), .D(out_0));
  FGNFET fgnfet_3 (.G(in_0), .D(fgnfet_1_s), .S(1'b0));
endmodule

/* Test case test_XOR:
in_0 in_1 out_0
  0    0     0
  0    1     1
  1    0     1
  1    1     0
*/
